# Fritzing sketch editing assistant (saved by Fritzing 0.9.3b)
breadboards: 1

parts:
  S1 = Pushbutton [package="[THT]"]
  R1 = Rotary Potentiometer (Small) [maximum_resistance=100kΩ package=THT]
  S5 = Toggle Switch [package=THT]
  LED1 = LED - 5mm [color="Red (633nm)" package="5 mm [THT]"]
  Part1 = Arduino Uno (Rev3) - ICSP
  R2 = Resistor [tolerance=±5% resistance=220 package=THT]
  R3 = Resistor [tolerance=±5% resistance=220 package=THT]
  S6 = Pushbutton [package="[THT]"]
  R4 = Resistor [tolerance=±5% resistance=220 package=THT]
  S7 = Pushbutton [package="[THT]"]
  R5 = Resistor [tolerance=±5% resistance=220 package=THT]
  S8 = Pushbutton [package="[THT]"]
  R6 = Resistor [tolerance=±5% resistance=220 package=THT]

nets:
  N1: S1.Pin_1, S1.Pin_2, R1.leg2, S5.L1, Part1.5V, S6.Pin_1, S6.Pin_2, S7.Pin_1, S7.Pin_2, S8.Pin_1, S8.Pin_2
  N2: S1.Pin_3, S1.Pin_4, Part1.D5_PWM, R3.Pin_1
  N3: R1.leg1, S5.L2, Part1.GND, R2.Pin_0, R3.Pin_0, R4.Pin_0, R5.Pin_0, R6.Pin_0
  N4: R1.wiper, Part1.ICSP_MISO, Part1.D12/MISO
  N5: S5.COM, Part1.D3_PWM
  N6: LED1.cathode, R2.Pin_1
  N7: Part1.D8, S8.Pin_3, S8.Pin_4, R6.Pin_1
  N8: Part1.D6_PWM, S6.Pin_3, S6.Pin_4, R4.Pin_1
  N9: Part1.D7, S7.Pin_3, S7.Pin_4, R5.Pin_1
